# Fritzing sketch tandon air (saved by Fritzing 0.9.3b)
breadboards: 1

parts:
  WeMos_D1_Mini1 = WeMos D1 Mini
  U1 = POT [package=pot_mammoth]
  U2 = LCD-16X2 [package=lcd-16x2_noholes]
  J1 = Piezo Speaker

nets:
  N1: WeMos_D1_Mini1.D1, J1.pin2
  N2: WeMos_D1_Mini1.D2, U2.RS
  N3: WeMos_D1_Mini1.D5, U2.DB4
  N4: WeMos_D1_Mini1.D6, U2.DB5
  N5: WeMos_D1_Mini1.D7, U2.DB6
  N6: WeMos_D1_Mini1.D8, U2.DB7
  N7: WeMos_D1_Mini1.G, U1.S, U2.R_W, U2.K, J1.pin1
  N8: U1.A, U2.VO
  N9: U1.E, U2.VDD, U2.A
